// Logisim project Obligatorio.circ as structural Verilog: 12 circuits, main circuit main
module main (
);

  wire Abajo_out, Arriba_out, Start_out, Stop_out;
  wire [2:0] paleta_1_out_4;
  wire [3:0] matriz_1_numperdidas;
  wire [7:0] matriz_1_x0, matriz_1_x1, matriz_1_x2, matriz_1_x3, matriz_1_x4, matriz_1_x5, matriz_1_x6,
       matriz_1_x7, matriz_1_x8, matriz_1_x9, matriz_1_x10, matriz_1_x11, matriz_1_x12, matriz_1_x13,
       matriz_1_x14, matriz_1_x15, paleta_1_pospaleta;

  Button Arriba (.out(Arriba_out));
  Button Abajo (.out(Abajo_out));
  Paleta paleta_1 (.Abajo(Abajo_out), .Arriba(Arriba_out), .PosPaleta(paleta_1_pospaleta), .out_4(paleta_1_out_4));
  Button Start (.out(Start_out));
  Button Stop (.out(Stop_out));
  DotMatrix #(.matrixcols(16), .matrixrows(8)) dotmatrix_1 (
    .col0(matriz_1_x0), .col1(matriz_1_x1), .col2(matriz_1_x2), .col3(matriz_1_x3), .col4(matriz_1_x4),
    .col5(matriz_1_x5), .col6(matriz_1_x6), .col7(matriz_1_x7), .col8(matriz_1_x8), .col9(matriz_1_x9),
    .col10(matriz_1_x10), .col11(matriz_1_x11), .col12(matriz_1_x12), .col13(matriz_1_x13),
    .col14(matriz_1_x14), .col15(matriz_1_x15));
  Matriz matriz_1 (
    .Stop(Stop_out), .paleta(paleta_1_out_4), .Start(Start_out), .PosPaleta(paleta_1_pospaleta),
    .x0(matriz_1_x0), .x1(matriz_1_x1), .x2(matriz_1_x2), .x3(matriz_1_x3), .x4(matriz_1_x4),
    .x5(matriz_1_x5), .x6(matriz_1_x6), .x7(matriz_1_x7), .x8(matriz_1_x8), .x9(matriz_1_x9),
    .x10(matriz_1_x10), .x11(matriz_1_x11), .x12(matriz_1_x12), .x13(matriz_1_x13), .x14(matriz_1_x14),
    .x15(matriz_1_x15), .NumPerdidas(matriz_1_numperdidas));
  Hex_Digit_Display hex_digit_display_1 (.value(matriz_1_numperdidas));  // open: dp

  // Notes on the sheet:
  //   Botones de control de paleta
  //   Vidas perdidas
  //   (Si se pierde 8 veces acabará el juego)
endmodule

module contador (
  input  [2:0] s0,
  input  Reset,
  input  NoColisiono,
  output Y2,
  output Y1,
  output Y0,
  output EstadoX,
  output X3,
  output X2,
  output X1,
  output X0
);

  wire and_1_out, and_2_out, and_3_out, clock_1_out, conty_1_d0, d_ff_1_q, d_ff_2_q, d_ff_3_q, d_ff_4_q,
       d_ff_5_q, d_ff_6_q, d_ff_7_q, d_ff_8_q, d_ff_9_q, or_1_out, or_2_out, or_3_out, or_4_out, or_5_out;

  Clock clock_1 (.out(clock_1_out));
  D_Flip_Flop d_ff_1 (.D(conty_1_d0), .clk(clock_1_out), .Q(d_ff_1_q), .reset(Reset));  // open: Qn, preset
  D_Flip_Flop d_ff_2 (.D(EstadoX), .clk(clock_1_out), .Q(d_ff_2_q), .reset(or_1_out));  // open: Qn, preset
  or or_1 (or_1_out, Reset, NoColisiono);
  and and_1 (and_1_out, Reset, s0[2]);
  D_Flip_Flop d_ff_3 (.D(Y2), .clk(clock_1_out), .Q(d_ff_3_q), .preset(and_1_out), .reset(Reset));  // open: Qn
  D_Flip_Flop d_ff_4 (.D(X3), .clk(clock_1_out), .Q(d_ff_4_q), .reset(or_2_out));  // open: Qn, preset
  or or_2 (or_2_out, Reset, NoColisiono);
  D_Flip_Flop d_ff_5 (.D(X2), .clk(clock_1_out), .Q(d_ff_5_q), .reset(or_3_out));  // open: Qn, preset
  and and_2 (and_2_out, Reset, s0[1]);
  D_Flip_Flop d_ff_6 (.D(Y1), .clk(clock_1_out), .Q(d_ff_6_q), .preset(and_2_out), .reset(Reset));  // open: Qn
  ContY conty_1 (
    .q0(d_ff_1_q), .q1(d_ff_3_q), .q2(d_ff_6_q), .q3(d_ff_7_q), .d0(conty_1_d0), .d1(Y2), .d2(Y1), .d3(Y0));
  or or_3 (or_3_out, Reset, NoColisiono);
  and and_3 (and_3_out, Reset, s0[0]);
  D_Flip_Flop d_ff_7 (.D(Y0), .clk(clock_1_out), .Q(d_ff_7_q), .preset(and_3_out), .reset(Reset));  // open: Qn
  D_Flip_Flop d_ff_8 (.D(X1), .clk(clock_1_out), .Q(d_ff_8_q), .reset(or_4_out));  // open: Qn, preset
  or or_4 (or_4_out, Reset, NoColisiono);
  ContX contx_1 (
    .q0(d_ff_2_q), .q1(d_ff_4_q), .q2(d_ff_5_q), .q3(d_ff_8_q), .q4(d_ff_9_q), .d0(EstadoX), .d1(X3),
    .d2(X2), .d3(X1), .d4(X0));
  D_Flip_Flop d_ff_9 (.D(X0), .clk(clock_1_out), .Q(d_ff_9_q), .reset(or_5_out));  // open: Qn, preset
  or or_5 (or_5_out, Reset, NoColisiono);

  // Notes on the sheet:
  //   Reset y
  //   Reset X
endmodule

module Matriz (
  input  Stop,
  input  [2:0] paleta,
  input  Start,
  input  [7:0] PosPaleta,
  output [7:0] x0,
  output [7:0] x1,
  output [7:0] x2,
  output [7:0] x3,
  output [7:0] x4,
  output [7:0] x5,
  output [7:0] x6,
  output [7:0] x7,
  output [7:0] x8,
  output [7:0] x9,
  output [7:0] x10,
  output [7:0] x11,
  output [7:0] x12,
  output [7:0] x13,
  output [7:0] x14,
  output [7:0] x15,
  output [3:0] NumPerdidas
);

  wire and_1_out, and_2_out, colisiondetecta_1_colision, comparator_1_eq, comparator_2_eq, comparator_3_eq,
       comparator_4_eq, comparator_5_eq, contador_1_y0, contador_1_y1, contador_1_y2, d_ff_1_q,
       decodificadorx_1_s0, decodificadorx_1_s1, decodificadorx_1_s2, decodificadorx_1_s3,
       decodificadorx_1_s4, decodificadorx_1_s5, decodificadorx_1_s6, decodificadorx_1_s7,
       decodificadorx_1_s8, decodificadorx_1_s9, decodificadorx_1_s10, decodificadorx_1_s11,
       decodificadorx_1_s12, decodificadorx_1_s13, decodificadorx_1_s14, decodificadorx_1_s15, DecoY_s0,
       DecoY_s1, DecoY_s2, DecoY_s3, DecoY_s4, DecoY_s5, DecoY_s6, DecoY_s7, not_1_out, or_2_out, or_3_out,
       or_4_out;
  wire [3:0] bitadder_1_out;
  wire [4:0] contador_1_x0;
  wire [7:0] bitadder_2_out, COL0_out_17, COL1_out_17, COL2_out_17, COL3_out_17, COL4_out_17, COL5_out_17,
       COL6_out_17, COL7_out_17, COL8_out_17, COL09_out_17, COL10_out_17, COL11_out_17, COL12_out_17,
       COL13_out_17, COL14_out_17, COL15_out_17;

  assign x0 = PosPaleta | COL0_out_17;  // OR_Gate or_1, 8 bits wide
  Multiplexer #(.width(8)) multiplexer_1 (.in0({8{1'b0}}), .in1(COL1_out_17), .out(x1), .sel(d_ff_1_q));
  not not_1 (not_1_out, d_ff_1_q);
  Multiplexer #(.width(8)) multiplexer_2 (.in0({8{1'b0}}), .in1(COL2_out_17), .out(x2), .sel(d_ff_1_q));
  D_Flip_Flop d_ff_1 (.Q(d_ff_1_q), .preset(Start), .reset(or_2_out));  // open: D, clk, Qn
  or or_2 (or_2_out, Stop, comparator_5_eq);
  contador contador_1 (
    .s0(paleta), .Reset(not_1_out), .NoColisiono(and_2_out), .Y2(contador_1_y2), .Y1(contador_1_y1),
    .Y0(contador_1_y0), .EstadoX(contador_1_x0[4]), .X3(contador_1_x0[3]), .X2(contador_1_x0[2]),
    .X1(contador_1_x0[1]), .X0(contador_1_x0[0]));
  BitAdder bitadder_1 (.in0(x0), .out(bitadder_1_out));
  Multiplexer #(.width(8)) multiplexer_3 (.in0({8{1'b0}}), .in1(COL3_out_17), .out(x3), .sel(d_ff_1_q));
  Comparator #(.mode("unsigned"), .width(5)) comparator_1 (
    .a(contador_1_x0), .b({5{1'b0}}), .eq(comparator_1_eq));  // open: gt, lt
  Comparator #(.mode("unsigned"), .width(5)) comparator_2 (
    .a(5'b10000), .b(contador_1_x0), .eq(comparator_2_eq));  // open: gt, lt
  Multiplexer #(.width(8)) multiplexer_4 (.in0({8{1'b0}}), .in1(COL4_out_17), .out(x4), .sel(d_ff_1_q));
  DecodificadorY DecoY (
    .f2(contador_1_y2), .f1(contador_1_y1), .f0(contador_1_y0), .s7(DecoY_s7), .s6(DecoY_s6), .s5(DecoY_s5),
    .s4(DecoY_s4), .s3(DecoY_s3), .s2(DecoY_s2), .s1(DecoY_s1), .s0(DecoY_s0));  // open: f7, f6, f5, f4, f3
  or or_3 (or_3_out, comparator_1_eq, comparator_2_eq);
  Comparator #(.mode("unsigned"), .width(4)) comparator_3 (
    .a(4'b0100), .b(bitadder_1_out), .eq(comparator_3_eq));  // open: gt, lt
  Multiplexer #(.width(8)) multiplexer_5 (.in0({8{1'b0}}), .in1(COL5_out_17), .out(x5), .sel(d_ff_1_q));
  DecodificadorX decodificadorx_1 (
    .xi3(contador_1_x0[3]), .xi2(contador_1_x0[2]), .xi1(contador_1_x0[1]), .xi0(contador_1_x0[0]),
    .s0(decodificadorx_1_s0), .s1(decodificadorx_1_s1), .s2(decodificadorx_1_s2), .s3(decodificadorx_1_s3),
    .s4(decodificadorx_1_s4), .s5(decodificadorx_1_s5), .s6(decodificadorx_1_s6), .s7(decodificadorx_1_s7),
    .s8(decodificadorx_1_s8), .s9(decodificadorx_1_s9), .s10(decodificadorx_1_s10),
    .s11(decodificadorx_1_s11), .s12(decodificadorx_1_s12), .s13(decodificadorx_1_s13),
    .s14(decodificadorx_1_s14), .s15(decodificadorx_1_s15));
  and and_1 (and_1_out, or_3_out, comparator_3_eq);
  Multiplexer #(.width(8)) multiplexer_6 (.in0({8{1'b0}}), .in1(COL6_out_17), .out(x6), .sel(d_ff_1_q));
  SelectordeColumna COL0 (
    .EntradaSelec(decodificadorx_1_s0), .in_2(DecoY_s7), .in_3(DecoY_s6), .in_4(DecoY_s5), .in_5(DecoY_s4),
    .in_6(DecoY_s3), .in_7(DecoY_s2), .in_8(DecoY_s1), .in_9(DecoY_s0), .out_10(COL0_out_17[7]),
    .out_11(COL0_out_17[6]), .out_12(COL0_out_17[5]), .out_13(COL0_out_17[4]), .out_14(COL0_out_17[3]),
    .out_15(COL0_out_17[2]), .out_16(COL0_out_17[1]), .out_17(COL0_out_17[0]));
  SelectordeColumna COL1 (
    .EntradaSelec(decodificadorx_1_s1), .in_2(DecoY_s7), .in_3(DecoY_s6), .in_4(DecoY_s5), .in_5(DecoY_s4),
    .in_6(DecoY_s3), .in_7(DecoY_s2), .in_8(DecoY_s1), .in_9(DecoY_s0), .out_10(COL1_out_17[7]),
    .out_11(COL1_out_17[6]), .out_12(COL1_out_17[5]), .out_13(COL1_out_17[4]), .out_14(COL1_out_17[3]),
    .out_15(COL1_out_17[2]), .out_16(COL1_out_17[1]), .out_17(COL1_out_17[0]));
  Multiplexer #(.width(8)) multiplexer_7 (.in0({8{1'b0}}), .in1(COL7_out_17), .out(x7), .sel(d_ff_1_q));
  Multiplexer #(.width(8)) multiplexer_8 (.in0({8{1'b0}}), .in1(COL8_out_17), .out(x8), .sel(d_ff_1_q));
  Multiplexer #(.width(8)) multiplexer_9 (.in0({8{1'b0}}), .in1(COL09_out_17), .out(x9), .sel(d_ff_1_q));
  SelectordeColumna COL4 (
    .EntradaSelec(decodificadorx_1_s4), .in_2(DecoY_s7), .in_3(DecoY_s6), .in_4(DecoY_s5), .in_5(DecoY_s4),
    .in_6(DecoY_s3), .in_7(DecoY_s2), .in_8(DecoY_s1), .in_9(DecoY_s0), .out_10(COL4_out_17[7]),
    .out_11(COL4_out_17[6]), .out_12(COL4_out_17[5]), .out_13(COL4_out_17[4]), .out_14(COL4_out_17[3]),
    .out_15(COL4_out_17[2]), .out_16(COL4_out_17[1]), .out_17(COL4_out_17[0]));
  SelectordeColumna COL3 (
    .EntradaSelec(decodificadorx_1_s3), .in_2(DecoY_s7), .in_3(DecoY_s6), .in_4(DecoY_s5), .in_5(DecoY_s4),
    .in_6(DecoY_s3), .in_7(DecoY_s2), .in_8(DecoY_s1), .in_9(DecoY_s0), .out_10(COL3_out_17[7]),
    .out_11(COL3_out_17[6]), .out_12(COL3_out_17[5]), .out_13(COL3_out_17[4]), .out_14(COL3_out_17[3]),
    .out_15(COL3_out_17[2]), .out_16(COL3_out_17[1]), .out_17(COL3_out_17[0]));
  SelectordeColumna COL2 (
    .EntradaSelec(decodificadorx_1_s2), .in_2(DecoY_s7), .in_3(DecoY_s6), .in_4(DecoY_s5), .in_5(DecoY_s4),
    .in_6(DecoY_s3), .in_7(DecoY_s2), .in_8(DecoY_s1), .in_9(DecoY_s0), .out_10(COL2_out_17[7]),
    .out_11(COL2_out_17[6]), .out_12(COL2_out_17[5]), .out_13(COL2_out_17[4]), .out_14(COL2_out_17[3]),
    .out_15(COL2_out_17[2]), .out_16(COL2_out_17[1]), .out_17(COL2_out_17[0]));
  ColisionDetecta colisiondetecta_1 (
    .x0(PosPaleta[0]), .y0(COL1_out_17[0]), .x1(PosPaleta[1]), .y1(COL1_out_17[1]), .x2(PosPaleta[2]),
    .y2(COL1_out_17[2]), .x3(PosPaleta[3]), .y3(COL1_out_17[3]), .x4(PosPaleta[4]), .y4(COL1_out_17[4]),
    .x5(PosPaleta[5]), .y5(COL1_out_17[5]), .x6(PosPaleta[6]), .y6(COL1_out_17[6]), .x7(PosPaleta[7]),
    .y7(COL1_out_17[7]), .colision(colisiondetecta_1_colision));
  Multiplexer #(.width(8)) multiplexer_10 (.in0({8{1'b0}}), .in1(COL10_out_17), .out(x10), .sel(d_ff_1_q));
  Comparator #(.mode("unsigned")) comparator_4 (.a(bitadder_2_out), .b(8'h3), .eq(comparator_4_eq));  // open: gt, lt
  Multiplexer #(.width(8)) multiplexer_11 (.in0({8{1'b0}}), .in1(COL11_out_17), .out(x11), .sel(d_ff_1_q));
  SelectordeColumna COL7 (
    .EntradaSelec(decodificadorx_1_s7), .in_2(DecoY_s7), .in_3(DecoY_s6), .in_4(DecoY_s5), .in_5(DecoY_s4),
    .in_6(DecoY_s3), .in_7(DecoY_s2), .in_8(DecoY_s1), .in_9(DecoY_s0), .out_10(COL7_out_17[7]),
    .out_11(COL7_out_17[6]), .out_12(COL7_out_17[5]), .out_13(COL7_out_17[4]), .out_14(COL7_out_17[3]),
    .out_15(COL7_out_17[2]), .out_16(COL7_out_17[1]), .out_17(COL7_out_17[0]));
  SelectordeColumna COL6 (
    .EntradaSelec(decodificadorx_1_s6), .in_2(DecoY_s7), .in_3(DecoY_s6), .in_4(DecoY_s5), .in_5(DecoY_s4),
    .in_6(DecoY_s3), .in_7(DecoY_s2), .in_8(DecoY_s1), .in_9(DecoY_s0), .out_10(COL6_out_17[7]),
    .out_11(COL6_out_17[6]), .out_12(COL6_out_17[5]), .out_13(COL6_out_17[4]), .out_14(COL6_out_17[3]),
    .out_15(COL6_out_17[2]), .out_16(COL6_out_17[1]), .out_17(COL6_out_17[0]));
  SelectordeColumna COL5 (
    .EntradaSelec(decodificadorx_1_s5), .in_2(DecoY_s7), .in_3(DecoY_s6), .in_4(DecoY_s5), .in_5(DecoY_s4),
    .in_6(DecoY_s3), .in_7(DecoY_s2), .in_8(DecoY_s1), .in_9(DecoY_s0), .out_10(COL5_out_17[7]),
    .out_11(COL5_out_17[6]), .out_12(COL5_out_17[5]), .out_13(COL5_out_17[4]), .out_14(COL5_out_17[3]),
    .out_15(COL5_out_17[2]), .out_16(COL5_out_17[1]), .out_17(COL5_out_17[0]));
  and and_2 (and_2_out, comparator_4_eq, colisiondetecta_1_colision);
  Multiplexer #(.width(8)) multiplexer_12 (.in0({8{1'b0}}), .in1(COL12_out_17), .out(x12), .sel(d_ff_1_q));
  Multiplexer #(.width(8)) multiplexer_13 (.in0({8{1'b0}}), .in1(COL13_out_17), .out(x13), .sel(d_ff_1_q));
  or or_4 (or_4_out, Stop, comparator_5_eq);
  Multiplexer #(.width(8)) multiplexer_14 (.in0({8{1'b0}}), .in1(COL14_out_17), .out(x14), .sel(d_ff_1_q));
  SelectordeColumna COL11 (
    .EntradaSelec(decodificadorx_1_s11), .in_2(DecoY_s7), .in_3(DecoY_s6), .in_4(DecoY_s5), .in_5(DecoY_s4),
    .in_6(DecoY_s3), .in_7(DecoY_s2), .in_8(DecoY_s1), .in_9(DecoY_s0), .out_10(COL11_out_17[7]),
    .out_11(COL11_out_17[6]), .out_12(COL11_out_17[5]), .out_13(COL11_out_17[4]), .out_14(COL11_out_17[3]),
    .out_15(COL11_out_17[2]), .out_16(COL11_out_17[1]), .out_17(COL11_out_17[0]));
  SelectordeColumna COL10 (
    .EntradaSelec(decodificadorx_1_s10), .in_2(DecoY_s7), .in_3(DecoY_s6), .in_4(DecoY_s5), .in_5(DecoY_s4),
    .in_6(DecoY_s3), .in_7(DecoY_s2), .in_8(DecoY_s1), .in_9(DecoY_s0), .out_10(COL10_out_17[7]),
    .out_11(COL10_out_17[6]), .out_12(COL10_out_17[5]), .out_13(COL10_out_17[4]), .out_14(COL10_out_17[3]),
    .out_15(COL10_out_17[2]), .out_16(COL10_out_17[1]), .out_17(COL10_out_17[0]));
  SelectordeColumna COL09 (
    .EntradaSelec(decodificadorx_1_s9), .in_2(DecoY_s7), .in_3(DecoY_s6), .in_4(DecoY_s5), .in_5(DecoY_s4),
    .in_6(DecoY_s3), .in_7(DecoY_s2), .in_8(DecoY_s1), .in_9(DecoY_s0), .out_10(COL09_out_17[7]),
    .out_11(COL09_out_17[6]), .out_12(COL09_out_17[5]), .out_13(COL09_out_17[4]), .out_14(COL09_out_17[3]),
    .out_15(COL09_out_17[2]), .out_16(COL09_out_17[1]), .out_17(COL09_out_17[0]));
  Multiplexer #(.width(8)) multiplexer_15 (.in0({8{1'b0}}), .in1(COL15_out_17), .out(x15), .sel(d_ff_1_q));
  CuentaPerdidas cuentaperdidas_1 (.Nocolision(and_1_out), .ResetNumGanadas(or_4_out), .NumPerdidas4Pin(NumPerdidas));
  Comparator #(.mode("unsigned"), .width(4)) comparator_5 (
    .a(NumPerdidas), .b(4'b1000), .eq(comparator_5_eq));  // open: gt, lt
  BitAdder bitadder_2 (
    .in0(x0), .in1(x1), .in2(x2), .in3(x3), .in4(x4), .in5(x5), .in6(x6), .in7(x7), .in8(x8), .in9(x9),
    .in10(x10), .in11(x11), .in12(x12), .in13(x13), .in14(x14), .in15(x15), .out(bitadder_2_out));
  SelectordeColumna COL15 (
    .EntradaSelec(decodificadorx_1_s15), .in_2(DecoY_s7), .in_3(DecoY_s6), .in_4(DecoY_s5), .in_5(DecoY_s4),
    .in_6(DecoY_s3), .in_7(DecoY_s2), .in_8(DecoY_s1), .in_9(DecoY_s0), .out_10(COL15_out_17[7]),
    .out_11(COL15_out_17[6]), .out_12(COL15_out_17[5]), .out_13(COL15_out_17[4]), .out_14(COL15_out_17[3]),
    .out_15(COL15_out_17[2]), .out_16(COL15_out_17[1]), .out_17(COL15_out_17[0]));
  SelectordeColumna COL14 (
    .EntradaSelec(decodificadorx_1_s14), .in_2(DecoY_s7), .in_3(DecoY_s6), .in_4(DecoY_s5), .in_5(DecoY_s4),
    .in_6(DecoY_s3), .in_7(DecoY_s2), .in_8(DecoY_s1), .in_9(DecoY_s0), .out_10(COL14_out_17[7]),
    .out_11(COL14_out_17[6]), .out_12(COL14_out_17[5]), .out_13(COL14_out_17[4]), .out_14(COL14_out_17[3]),
    .out_15(COL14_out_17[2]), .out_16(COL14_out_17[1]), .out_17(COL14_out_17[0]));
  SelectordeColumna COL13 (
    .EntradaSelec(decodificadorx_1_s13), .in_2(DecoY_s7), .in_3(DecoY_s6), .in_4(DecoY_s5), .in_5(DecoY_s4),
    .in_6(DecoY_s3), .in_7(DecoY_s2), .in_8(DecoY_s1), .in_9(DecoY_s0), .out_10(COL13_out_17[7]),
    .out_11(COL13_out_17[6]), .out_12(COL13_out_17[5]), .out_13(COL13_out_17[4]), .out_14(COL13_out_17[3]),
    .out_15(COL13_out_17[2]), .out_16(COL13_out_17[1]), .out_17(COL13_out_17[0]));
  SelectordeColumna COL12 (
    .EntradaSelec(decodificadorx_1_s12), .in_2(DecoY_s7), .in_3(DecoY_s6), .in_4(DecoY_s5), .in_5(DecoY_s4),
    .in_6(DecoY_s3), .in_7(DecoY_s2), .in_8(DecoY_s1), .in_9(DecoY_s0), .out_10(COL12_out_17[7]),
    .out_11(COL12_out_17[6]), .out_12(COL12_out_17[5]), .out_13(COL12_out_17[4]), .out_14(COL12_out_17[3]),
    .out_15(COL12_out_17[2]), .out_16(COL12_out_17[1]), .out_17(COL12_out_17[0]));
  SelectordeColumna COL8 (
    .EntradaSelec(decodificadorx_1_s8), .in_2(DecoY_s7), .in_3(DecoY_s6), .in_4(DecoY_s5), .in_5(DecoY_s4),
    .in_6(DecoY_s3), .in_7(DecoY_s2), .in_8(DecoY_s1), .in_9(DecoY_s0), .out_10(COL8_out_17[7]),
    .out_11(COL8_out_17[6]), .out_12(COL8_out_17[5]), .out_13(COL8_out_17[4]), .out_14(COL8_out_17[3]),
    .out_15(COL8_out_17[2]), .out_16(COL8_out_17[1]), .out_17(COL8_out_17[0]));
endmodule

module DecodificadorY (
  input  f7,
  input  f6,
  input  f5,
  input  f4,
  input  f3,
  input  f2,
  input  f1,
  input  f0,
  output s7,
  output s6,
  output s5,
  output s4,
  output s3,
  output s2,
  output s1,
  output s0
);

  wire not_1_out, not_2_out, not_3_out, not_4_out, not_5_out, not_6_out, not_7_out, not_8_out;

  not not_1 (not_1_out, f7);
  not not_2 (not_2_out, f6);
  not not_3 (not_3_out, f5);
  not not_4 (not_4_out, f4);
  not not_5 (not_5_out, f3);
  not not_6 (not_6_out, f2);
  not not_7 (not_7_out, f1);
  not not_8 (not_8_out, f0);
  and and_1 (s7, not_8_out, not_7_out, not_6_out, not_5_out, not_4_out, not_3_out, not_2_out, not_1_out);
  and and_2 (s6, f0, not_7_out, not_6_out, not_5_out, not_4_out, not_3_out, not_2_out, not_1_out);
  and and_3 (s5, f1, not_8_out, not_6_out, not_5_out, not_4_out, not_3_out, not_2_out, not_1_out);
  and and_4 (s4, f1, f0, not_6_out, not_5_out, not_4_out, not_3_out, not_2_out, not_1_out);
  and and_5 (s3, f2, not_8_out, not_7_out, not_5_out, not_4_out, not_3_out, not_2_out, not_1_out);
  and and_6 (s2, f2, f0, not_7_out, not_5_out, not_4_out, not_3_out, not_2_out, not_1_out);
  and and_7 (s1, f2, f1, not_8_out, not_5_out, not_4_out, not_3_out, not_2_out, not_1_out);
  and and_8 (s0, f2, f1, f0, not_5_out, not_4_out, not_3_out, not_2_out, not_1_out);
endmodule

module SelectordeColumna (
  input  EntradaSelec,
  input  in_2,
  input  in_3,
  input  in_4,
  input  in_5,
  input  in_6,
  input  in_7,
  input  in_8,
  input  in_9,
  output out_10,
  output out_11,
  output out_12,
  output out_13,
  output out_14,
  output out_15,
  output out_16,
  output out_17
);

  and and_1 (out_10, in_2, EntradaSelec);
  and and_2 (out_11, in_3, EntradaSelec);
  and and_3 (out_12, in_4, EntradaSelec);
  and and_4 (out_13, in_5, EntradaSelec);
  and and_5 (out_14, in_6, EntradaSelec);
  and and_6 (out_15, in_7, EntradaSelec);
  and and_7 (out_16, in_8, EntradaSelec);
  and and_8 (out_17, in_9, EntradaSelec);
endmodule

module DecodificadorX (
  input  xi3,
  input  xi2,
  input  xi1,
  input  xi0,
  output s0,
  output s1,
  output s2,
  output s3,
  output s4,
  output s5,
  output s6,
  output s7,
  output s8,
  output s9,
  output s10,
  output s11,
  output s12,
  output s13,
  output s14,
  output s15
);

  wire not_1_out, not_2_out, not_3_out, not_4_out, not_5_out, not_6_out, not_7_out, not_8_out, not_9_out,
       not_10_out, not_11_out, not_12_out;

  not not_1 (not_1_out, xi3);
  not not_2 (not_2_out, xi2);
  not not_3 (not_3_out, xi1);
  not not_4 (not_4_out, xi0);
  not not_5 (not_5_out, xi3);
  not not_6 (not_6_out, xi1);
  not not_7 (not_7_out, xi0);
  not not_8 (not_8_out, xi2);
  not not_9 (not_9_out, xi1);
  not not_10 (not_10_out, xi0);
  not not_11 (not_11_out, xi1);
  not not_12 (not_12_out, xi0);
  and and_1 (s0, not_1_out, not_2_out, not_3_out, not_4_out);
  and and_2 (s1, not_1_out, not_2_out, not_3_out, xi0);
  and and_3 (s2, not_1_out, not_2_out, xi1, not_4_out);
  and and_4 (s3, not_1_out, not_2_out, xi1, xi0);
  and and_5 (s4, not_5_out, xi2, not_6_out, not_7_out);
  and and_6 (s5, not_5_out, xi2, not_6_out, xi0);
  and and_7 (s6, not_5_out, xi2, xi1, not_7_out);
  and and_8 (s7, not_5_out, xi2, xi1, xi0);
  and and_9 (s8, xi3, not_8_out, not_9_out, not_10_out);
  and and_10 (s9, xi3, not_8_out, not_9_out, xi0);
  and and_11 (s10, xi3, not_8_out, xi1, not_10_out);
  and and_12 (s11, xi3, not_8_out, xi1, xi0);
  and and_13 (s12, xi3, xi2, not_11_out, not_12_out);
  and and_14 (s13, xi3, xi2, not_11_out, xi0);
  and and_15 (s14, xi3, xi2, xi1, not_12_out);
  and and_16 (s15, xi3, xi2, xi1, xi0);

  // Notes on the sheet:
  //   Parte 1 del 0000 0001 0010 0011
  //   parte 2
  //   parte 3
  //   parte 4
endmodule

module Paleta (
  input  Abajo,
  input  Arriba,
  output [7:0] PosPaleta,
  output [2:0] out_4
);

  wire and_1_out, and_2_out, button_1_out, clock_1_out, comparator_1_gt, comparator_2_gt, or_1_out;
  wire [2:0] adder_1_out, multiplexer_1_out, register_1_q, subtractor_1_out;

  Adder #(.width(3)) adder_1 (.a(3'b001), .b(register_1_q), .out(adder_1_out));  // open: cin, cout
  Subtractor #(.width(3)) subtractor_1 (.a(register_1_q), .b(3'b001), .out(subtractor_1_out));  // open: bin, bout
  and and_1 (and_1_out, comparator_1_gt, Abajo);
  Multiplexer #(.width(3)) multiplexer_1 (
    .in0(adder_1_out), .in1(subtractor_1_out), .out(multiplexer_1_out), .sel(Arriba));
  Clock clock_1 (.out(clock_1_out));
  and and_2 (and_2_out, comparator_2_gt, Arriba);
  Register #(.width(3)) register_1 (
    .D(multiplexer_1_out), .en(or_1_out), .clk(clock_1_out), .Q(register_1_q), .clr(button_1_out));
  or or_1 (or_1_out, and_1_out, and_2_out);
  Button button_1 (.out(button_1_out));
  Comparator #(.mode("unsigned"), .width(3)) comparator_1 (
    .a(3'b101), .b(register_1_q), .gt(comparator_1_gt));  // open: eq, lt
  Comparator #(.mode("unsigned"), .width(3)) comparator_2 (
    .a(register_1_q), .b(3'b000), .gt(comparator_2_gt));  // open: eq, lt
  Adder #(.width(3)) adder_2 (.a(3'b010), .b(register_1_q), .out(out_4));  // open: cin, cout
  DecodificadorPaleta decodificadorpaleta_1 (
    .x0(register_1_q[2]), .x1(register_1_q[1]), .x2(register_1_q[0]), .Paleta(PosPaleta));
endmodule

module DecodificadorPaleta (
  input  x0,
  input  x1,
  input  x2,
  output [7:0] Paleta
);

  wire and_3_out, and_4_out, and_5_out, and_6_out, and_7_out, and_8_out, and_9_out, and_10_out, not_1_out,
       not_2_out, not_3_out;

  not not_1 (not_1_out, x0);
  not not_2 (not_2_out, x1);
  not not_3 (not_3_out, x2);
  and and_1 (Paleta[7], not_1_out, not_2_out, not_3_out);
  and and_2 (Paleta[6], not_1_out, not_2_out);
  and and_3 (and_3_out, not_1_out, not_2_out);
  and and_4 (and_4_out, not_1_out, not_3_out);
  and and_5 (and_5_out, not_1_out, x2);
  and and_6 (and_6_out, not_1_out, x1);
  and and_7 (and_7_out, not_1_out, x1);
  and and_8 (and_8_out, x0, not_2_out, not_3_out);
  and and_9 (and_9_out, not_1_out, x1, x2);
  and and_10 (and_10_out, x0, not_2_out);
  and and_11 (Paleta[1], x0, not_2_out);
  and and_12 (Paleta[0], x0, not_2_out, x2);
  or or_1 (Paleta[5], and_3_out, and_4_out);
  or or_2 (Paleta[4], and_5_out, and_6_out);
  or or_3 (Paleta[3], and_7_out, and_8_out);
  or or_4 (Paleta[2], and_9_out, and_10_out);
endmodule

module ContY (
  input  q0,
  input  q1,
  input  q2,
  input  q3,
  output d0,
  output d1,
  output d2,
  output d3
);

  wire and_1_out, and_2_out, and_3_out, and_4_out, and_5_out, and_6_out, and_7_out, and_8_out, and_9_out,
       and_10_out, and_11_out, and_12_out, and_13_out, and_14_out, not_1_out, not_2_out, not_3_out, not_4_out;

  not not_1 (not_1_out, q0);
  not not_2 (not_2_out, q1);
  not not_3 (not_3_out, q2);
  not not_4 (not_4_out, q3);
  and and_1 (and_1_out, not_1_out, not_2_out, not_3_out, not_4_out);
  and and_2 (and_2_out, q0, not_2_out, q2);
  and and_3 (and_3_out, q0, q1, not_3_out);
  and and_4 (and_4_out, q0, not_2_out, q3);
  and and_5 (and_5_out, q1, q3);
  and and_6 (and_6_out, q1, q2);
  and and_7 (and_7_out, q0, q2, q3);
  and and_8 (and_8_out, q0, q1);
  and and_9 (and_9_out, not_1_out, q2, q3);
  and and_10 (and_10_out, not_1_out, q1, not_3_out, not_4_out);
  and and_11 (and_11_out, q0, not_3_out, q3);
  and and_12 (and_12_out, q0, q2, not_4_out);
  and and_13 (and_13_out, q1, q2, q3);
  and and_14 (and_14_out, q0, q1, q2);
  or or_1 (d0, and_1_out, and_2_out, and_3_out, and_4_out);
  or or_2 (d1, and_5_out, and_6_out, and_7_out, and_8_out);
  or or_3 (d2, and_9_out, and_10_out, and_11_out, and_12_out, and_13_out);
  or or_4 (d3, not_4_out, and_14_out);
endmodule

module ContX (
  input  q0,
  input  q1,
  input  q2,
  input  q3,
  input  q4,
  output d0,
  output d1,
  output d2,
  output d3,
  output d4
);

  wire and_1_out, and_2_out, and_3_out, and_4_out, and_5_out, and_6_out, and_7_out, and_8_out, and_9_out,
       and_10_out, and_11_out, and_12_out, and_13_out, and_14_out, and_15_out, and_16_out, and_17_out,
       and_18_out, and_19_out, and_20_out, and_21_out, and_22_out, and_23_out, and_24_out, not_1_out,
       not_2_out, not_3_out;

  not not_1 (not_1_out, q0);
  not not_2 (not_2_out, q2);
  not not_3 (not_3_out, q3);
  not not_4 (d4, q4);
  and and_1 (and_1_out, q1, q2, q3, q4);
  and and_2 (and_2_out, q0, q4);
  and and_3 (and_3_out, q0, q3);
  and and_4 (and_4_out, q0, q2);
  and and_5 (and_5_out, q0, q1);
  and and_6 (and_6_out, not_1_out, q2, q3, q4);
  and and_7 (and_7_out, not_1_out, q1);
  and and_8 (and_8_out, q1, q4);
  and and_9 (and_9_out, q1, q3);
  and and_10 (and_10_out, q1, q2);
  and and_11 (and_11_out, not_1_out, not_2_out, q3, q4);
  and and_12 (and_12_out, q0, q1, not_2_out, not_3_out, d4);
  and and_13 (and_13_out, not_1_out, q2, not_3_out);
  and and_14 (and_14_out, not_1_out, q2, d4);
  and and_15 (and_15_out, not_1_out, q1, q2);
  and and_16 (and_16_out, q2, not_3_out, q4);
  and and_17 (and_17_out, q2, q3, d4);
  and and_18 (and_18_out, q0, q2, q4);
  and and_19 (and_19_out, not_1_out, not_3_out, q4);
  and and_20 (and_20_out, not_1_out, q3, d4);
  and and_21 (and_21_out, q0, q3, q4);
  and and_22 (and_22_out, q0, q2, not_3_out, d4);
  and and_23 (and_23_out, q0, q1, not_3_out, d4);
  and and_24 (and_24_out, not_1_out, q1, q2, q4);
  or or_1 (d0, and_1_out, and_2_out, and_3_out, and_4_out, and_5_out);
  or or_2 (d1, and_6_out, and_7_out, and_8_out, and_9_out, and_10_out);
  or or_3 (d2, and_11_out, and_12_out, and_13_out, and_14_out, and_15_out, and_16_out, and_17_out, and_18_out);
  or or_4 (d3, and_19_out, and_20_out, and_21_out, and_22_out, and_23_out, and_24_out);
endmodule

module ColisionDetecta (
  input  x0,
  input  y0,
  input  x1,
  input  y1,
  input  x2,
  input  y2,
  input  x3,
  input  y3,
  input  x4,
  input  y4,
  input  x5,
  input  y5,
  input  x6,
  input  y6,
  input  x7,
  input  y7,
  output colision
);

  wire and_1_out, and_2_out, and_3_out, and_4_out, and_5_out, and_6_out, and_7_out, and_8_out, and_9_out,
       and_10_out, and_11_out, and_12_out, and_13_out, and_14_out, and_15_out, and_16_out, and_17_out,
       and_18_out, and_19_out, and_20_out, and_21_out, and_22_out, and_23_out, and_24_out, and_25_out,
       and_26_out, and_27_out, and_28_out, not_1_out, not_2_out, not_3_out, not_4_out, not_5_out, not_6_out,
       not_7_out, not_8_out, not_9_out, not_10_out, not_11_out, not_12_out, not_13_out, not_14_out, or_1_out,
       or_2_out, or_3_out, or_4_out, or_5_out, or_6_out, or_7_out, or_9_out, or_10_out, or_11_out, or_12_out,
       or_13_out;

  not not_1 (not_1_out, y0);
  not not_2 (not_2_out, y1);
  not not_3 (not_3_out, y2);
  not not_4 (not_4_out, y3);
  not not_5 (not_5_out, y4);
  not not_6 (not_6_out, y5);
  not not_7 (not_7_out, y6);
  not not_8 (not_8_out, y7);
  and and_1 (and_1_out, x1, not_1_out, y1);
  and and_2 (and_2_out, x1, y0, not_2_out);
  and and_3 (and_3_out, x0, not_1_out, y1);
  and and_4 (and_4_out, x0, y0, not_2_out);
  and and_5 (and_5_out, x3, not_3_out, y3);
  and and_6 (and_6_out, x3, y2, not_4_out);
  and and_7 (and_7_out, x2, not_3_out, y3);
  and and_8 (and_8_out, x2, y2, not_4_out);
  and and_9 (and_9_out, x5, not_5_out, y5);
  and and_10 (and_10_out, x5, y4, not_6_out);
  and and_11 (and_11_out, x4, not_5_out, y5);
  and and_12 (and_12_out, x4, y4, not_6_out);
  and and_13 (and_13_out, x7, not_7_out, y7);
  and and_14 (and_14_out, x7, y6, not_8_out);
  and and_15 (and_15_out, x6, not_7_out, y7);
  and and_16 (and_16_out, x6, y6, not_8_out);
  or or_1 (or_1_out, and_1_out, and_2_out, and_3_out, and_4_out);
  or or_2 (or_2_out, and_5_out, and_6_out, and_7_out, and_8_out);
  or or_3 (or_3_out, and_9_out, and_10_out, and_11_out, and_12_out);
  or or_4 (or_4_out, and_13_out, and_14_out, and_15_out, and_16_out);
  or or_5 (or_5_out, or_1_out, or_2_out);
  or or_6 (or_6_out, or_3_out, or_4_out);
  or or_7 (or_7_out, or_5_out, or_6_out);
  or or_8 (colision, or_7_out, or_13_out);
  not not_9 (not_9_out, y1);
  not not_10 (not_10_out, y2);
  not not_11 (not_11_out, y3);
  not not_12 (not_12_out, y4);
  not not_13 (not_13_out, y5);
  not not_14 (not_14_out, y6);
  and and_17 (and_17_out, x2, not_9_out, y2);
  and and_18 (and_18_out, x2, y1, not_10_out);
  and and_19 (and_19_out, x1, not_9_out, y2);
  and and_20 (and_20_out, x1, y1, not_10_out);
  and and_21 (and_21_out, x4, not_11_out, y4);
  and and_22 (and_22_out, x4, y3, not_12_out);
  and and_23 (and_23_out, x3, not_11_out, y4);
  and and_24 (and_24_out, x3, y3, not_12_out);
  and and_25 (and_25_out, x6, not_13_out, y6);
  and and_26 (and_26_out, x6, y5, not_14_out);
  and and_27 (and_27_out, x5, not_13_out, y6);
  and and_28 (and_28_out, x5, y5, not_14_out);
  or or_9 (or_9_out, and_17_out, and_18_out, and_19_out, and_20_out);
  or or_10 (or_10_out, and_21_out, and_22_out, and_23_out, and_24_out);
  or or_11 (or_11_out, and_25_out, and_26_out, and_27_out, and_28_out);
  or or_12 (or_12_out, or_9_out, or_10_out);
  or or_13 (or_13_out, or_12_out, or_11_out);

  // Notes on the sheet:
  //   Colision total
endmodule

module CuentaPerdidas (
  input  Nocolision,
  input  ResetNumGanadas,
  output [3:0] NumPerdidas4Pin
);

  wire and_1_out, comparator_1_lt;
  wire [3:0] adder_1_out;

  and and_1 (and_1_out, comparator_1_lt, Nocolision);
  Adder #(.width(4)) adder_1 (.a(NumPerdidas4Pin), .b(4'b0001), .out(adder_1_out));  // open: cin, cout
  Comparator #(.mode("unsigned"), .width(4)) comparator_1 (
    .a(NumPerdidas4Pin), .b(4'b1000), .lt(comparator_1_lt));  // open: gt, eq
  Register #(.width(4)) register_1 (
    .D(adder_1_out), .en(and_1_out), .clk(and_1_out), .Q(NumPerdidas4Pin), .clr(ResetNumGanadas));
endmodule
